# Fritzing sketch LED_555 (saved by Fritzing 1.0.3b)
breadboards: 1

parts:
  U1 = 555 Timer [package="SO8 [SMD]"]  # not connected
  R1 = Resistor [tolerance=±5% resistance=47k package="0402 [SMD]"]
  C1 = Electrolytic Capacitor [capacitance=10μF voltage=16V package="0605 [SMD, electrolytic]"]
  R2 = Resistor [tolerance=±5% resistance=47k package="0402 [SMD]"]
  R3 = Resistor [tolerance=±5% resistance=470 package="0402 [SMD]"]
  VCC1 = Battery block 9V [internal_resistance=0.1Ω]
  LED1 = LED - 5mm [color="Red (633nm)" current=0.030A package="5 mm [THT]"]

nets:
  N1: R1.Pin_0, R2.Pin_1
  N2: R1.Pin_1, C1.+
  N3: C1.-, VCC1.-, LED1.cathode
  N4: R2.Pin_0, VCC1.+
  N5: R3.Pin_1, LED1.anode
